# Fritzing sketch OpenLDAT_Model1 (saved by Fritzing 0.9.4)
circuit board: 2.3cm x 4.1cm
breadboards: 1

parts:
  LED1 = LED - 5mm [color="Blue (525nm)" package="5 mm [THT]"]
  MCU = SparkFun Pro Micro
  Button = male pin header, 2 pins [form="♂ (male)"]
  R4 = Resistor [tolerance=±5% resistance=22k package=THT]
  R3 = Resistor [tolerance=±5% resistance=330k package=THT]
  R5 = Resistor [tolerance=±5% resistance=47k package=THT]
  R1 = Resistor [tolerance=±5% resistance=1k package=THT]
  R2 = Resistor [tolerance=±5% resistance=1M package=THT]
  PT19 = ALSPT19315C

nets:
  N1: LED1.cathode, R1.Pin_0
  N2: LED1.anode, MCU.6, MCU.7, Button.pin1, R2.Pin_0
  N3: MCU.GND, R3.Pin_1, R1.Pin_1, R2.Pin_1
  N4: MCU.4, Button.pin2
  N5: MCU.14, R4.Pin_1
  N6: MCU.15, R5.Pin_1
  N7: MCU.A0, PT19.OUT
  VCC: MCU.VCC, PT19.VCC
  N8: R4.Pin_0, R3.Pin_0, R5.Pin_0, PT19.GND

custom parts:
  SparkFun Pro Micro: The Pro Micro is similar to the Pro Mini except with an ATmega32U4 on board. The USB transceiver inside the 32U4 allows us to add USB connectivity on-board and do away with bulky external USB interface. Based on: https://github.com/unorthodox-engineers/unorthodox-arduino/blob/master/Unorthodox/fritzing/parts/Pro%20Micro.fzpz
  ALSPT19315C: Add a teeny analog light sensor, the ALS PT19 analog light sensor is a great way to upgrade a project that uses a photocell and needs RoHS compliance. Due to the high rejection ratio of infrared radiation, the spectral response of the ambient light sensor is close to that of human eyes. It's a pretty simple sensor - connect - to ground, + to 2.5V-5.5V or so to power it. Now measure the analog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
